// Logisim project RealAlu.circ as structural Verilog: 27 circuits, main circuit ArithUnit
module Mask (
  input  [7:0] A,
  input  [3:0] Choose_operation,
  input  [7:0] B,
  output [7:0] Result
);

  wire realalu_1_c, realalu_1_n, realalu_1_v, realalu_1_z, S;

  RealAlu realalu_1 (
    .Operation_Select(Choose_operation), .A(A), .B(B), .To_Mask(Result), .V(realalu_1_v), .N(realalu_1_n),
    .C(realalu_1_c), .Z(realalu_1_z), .EXEC(S));
  LED N (.in(realalu_1_n));
  LED C (.in(realalu_1_c));
  LED V (.in(realalu_1_v));
  LED Z (.in(realalu_1_z));
  Button EXEC (.out(S));

  // Other names for the same wires on the sheet: O[3:0] = Choose_operation

  // Notes on the sheet:
  //   Enter Data
  //   Logic Unit Operations
  //   0000 - A&B
  //   0001 - A|B
  //   0010 - !B  
  //   0011 - LSL B
  //   0100 - LSR B
  //   Titan ALU is propriety of LBC and BorellTech. Titan ALU is fully compatible with the Bayonetta Processor
  //   Arith Unit Operations
  //   0101 - A+B
  //   0110 - A-B
  //   0111 - B+1
  //   1000 - B-1
  //   1001 - A
endmodule

module RealAlu (
  input  [3:0] Operation_Select,
  input  [7:0] A,
  input  [7:0] B,
  input  EXEC,
  output [7:0] To_Mask,
  output V,
  output N,
  output C,
  output Z
);

  wire arithunit_1_c, arithunit_1_n, arithunit_1_z, logicunit_1_c, logicunit_1_n, logicunit_1_z,
       processor_enabler_1_out0, processor_enabler_1_out1, processor_enabler_1_out2,
       processor_enabler_1_out3, processor_enabler_1_out4, processor_enabler_1_out5,
       processor_enabler_1_out6, processor_enabler_1_out7, processor_enabler_aux_1_out0,
       processor_enabler_aux_1_out1, processor_enabler_aux_1_out2, processor_enabler_aux_1_out3,
       processor_enabler_aux_1_out4, processor_enabler_aux_1_out5, processor_enabler_aux_1_out6,
       processor_enabler_aux_1_out7;
  wire [7:0] and_1_out, arithunit_1_a, logicunit_1_logic_out, not_1_out, or_1_out;

  Processor_Enabler processor_enabler_1 (
    .Processor_Check(1'b1), .IN0(A[0]), .IN1(A[1]), .IN2(A[2]), .IN3(A[3]), .IN4(A[4]), .IN5(A[5]),
    .IN6(A[6]), .IN7(A[7]), .OUT0(processor_enabler_1_out0), .OUT1(processor_enabler_1_out1),
    .OUT2(processor_enabler_1_out2), .OUT3(processor_enabler_1_out3), .OUT4(processor_enabler_1_out4),
    .OUT5(processor_enabler_1_out5), .OUT6(processor_enabler_1_out6), .OUT7(processor_enabler_1_out7));
  ArithUnit arithunit_1 (
    .a0(processor_enabler_1_out0), .a1(processor_enabler_1_out1), .a2(processor_enabler_1_out2),
    .a3(processor_enabler_1_out3), .a4(processor_enabler_1_out4), .a5(processor_enabler_1_out5),
    .a6(processor_enabler_1_out6), .a7(processor_enabler_1_out7), .b0(processor_enabler_aux_1_out0),
    .b1(processor_enabler_aux_1_out1), .b2(processor_enabler_aux_1_out2), .b3(processor_enabler_aux_1_out3),
    .b4(processor_enabler_aux_1_out4), .b5(processor_enabler_aux_1_out5), .b6(processor_enabler_aux_1_out6),
    .b7(processor_enabler_aux_1_out7), .A(arithunit_1_a), .Operation(Operation_Select), .V(V),
    .C(arithunit_1_c), .Z(arithunit_1_z), .N(arithunit_1_n));
  Processor_Enabler_AUX processor_enabler_aux_1 (
    .Processor_Check(1'b1), .IN0(B[0]), .IN1(B[1]), .IN2(B[2]), .IN3(B[3]), .IN4(B[4]), .IN5(B[5]),
    .IN6(B[6]), .IN7(B[7]), .OUT0(processor_enabler_aux_1_out0), .OUT1(processor_enabler_aux_1_out1),
    .OUT2(processor_enabler_aux_1_out2), .OUT3(processor_enabler_aux_1_out3),
    .OUT4(processor_enabler_aux_1_out4), .OUT5(processor_enabler_aux_1_out5),
    .OUT6(processor_enabler_aux_1_out6), .OUT7(processor_enabler_aux_1_out7));
  assign and_1_out = logicunit_1_logic_out & not_1_out;  // AND_Gate and_1, 8 bits wide
  LogicUnit logicunit_1 (
    ._0(Operation_Select[0]), .in_2(Operation_Select[1]), ._3(Operation_Select[2]), .A(A), .B(B),
    .Logic_Out(logicunit_1_logic_out), .N(logicunit_1_n), .Z(logicunit_1_z), .C(logicunit_1_c));
  assign not_1_out = ~{8{Operation_Select[3]}};  // NOT_Gate not_1, 8 bits wide
  // Probe on or_1_out
  assign or_1_out = arithunit_1_a | and_1_out;  // OR_Gate or_1, 8 bits wide
  Instant_Calc_Memory instant_calc_memory_1 (
    .From_Calc_Unit(or_1_out), .Save(EXEC), .Clear(1'b0), .From_Volatile_Memory(To_Mask));
  or or_2 (C, arithunit_1_c, logicunit_1_c);
  or or_3 (Z, logicunit_1_z, arithunit_1_z);
  or or_4 (N, arithunit_1_n, logicunit_1_n);
endmodule

module ArithUnit (
  input  a0,
  input  a1,
  input  a2,
  input  a3,
  input  a4,
  input  a5,
  input  a6,
  input  a7,
  input  b0,
  input  b1,
  input  b2,
  input  b3,
  input  b4,
  input  b5,
  input  b6,
  input  b7,
  input  [3:0] Operation,
  output [7:0] A,
  output V,
  output C,
  output N,
  output Z
);

  wire arith_status_check_1_z, arith_unit_operation_select_1_ablank, arith_unit_operation_select_1_decrem,
       arith_unit_operation_select_1_increm, arith_unit_operation_select_1_somma,
       arith_unit_operation_select_1_sottrazione, b_increment_1_carry, button_1_out,
       intel_adder_inside_1_resto, or_1_out, or_3_out, processor_enabler_1_out0, processor_enabler_1_out1,
       processor_enabler_1_out2, processor_enabler_1_out3, processor_enabler_1_out4,
       processor_enabler_1_out5, processor_enabler_1_out6, processor_enabler_1_out7,
       processor_enabler_2_out0, processor_enabler_2_out1, processor_enabler_2_out2,
       processor_enabler_2_out3, processor_enabler_2_out4, processor_enabler_2_out5,
       processor_enabler_2_out6, processor_enabler_2_out7, processor_enabler_3_out0,
       processor_enabler_3_out1, processor_enabler_3_out2, processor_enabler_3_out3,
       processor_enabler_3_out4, processor_enabler_3_out5, processor_enabler_3_out6,
       processor_enabler_3_out7, processor_enabler_4_out0, processor_enabler_4_out1,
       processor_enabler_4_out2, processor_enabler_4_out3, processor_enabler_4_out4,
       processor_enabler_4_out5, processor_enabler_4_out6, processor_enabler_4_out7,
       processor_enabler_aux_1_out0, processor_enabler_aux_1_out1, processor_enabler_aux_1_out2,
       processor_enabler_aux_1_out3, processor_enabler_aux_1_out4, processor_enabler_aux_1_out5,
       processor_enabler_aux_1_out6, processor_enabler_aux_1_out7, processor_enabler_aux_2_out0,
       processor_enabler_aux_2_out1, processor_enabler_aux_2_out2, processor_enabler_aux_2_out3,
       processor_enabler_aux_2_out4, processor_enabler_aux_2_out5, processor_enabler_aux_2_out6,
       processor_enabler_aux_2_out7;
  wire [7:0] a_1_a, b_decrement_1_risultato, b_increment_1_b_1, cpl2_1_y0, intel_adder_inside_1_y0;

  Button button_1 (.out(button_1_out));
  Arith_Unit_Operation_Select arith_unit_operation_select_1 (
    ._0(Operation[0]), ._1(Operation[1]), ._2(Operation[2]), ._3(Operation[3]),
    .Somma(arith_unit_operation_select_1_somma), .Sottrazione(arith_unit_operation_select_1_sottrazione),
    .Increm(arith_unit_operation_select_1_increm), .Decrem(arith_unit_operation_select_1_decrem),
    .aBlank(arith_unit_operation_select_1_ablank));
  or or_1 (or_1_out, arith_unit_operation_select_1_somma, arith_unit_operation_select_1_sottrazione, arith_unit_operation_select_1_increm, arith_unit_operation_select_1_decrem, arith_unit_operation_select_1_ablank);
  A a_1 (.in_1({a7, a6, a5, a4, a3, a2, a1, a0}), .in_2(arith_unit_operation_select_1_ablank), .A(a_1_a));
  Processor_Enabler processor_enabler_1 (
    .Processor_Check(arith_unit_operation_select_1_somma), .IN0(a0), .IN1(a1), .IN2(a2), .IN3(a3), .IN4(a4),
    .IN5(a5), .IN6(a6), .IN7(a7), .OUT0(processor_enabler_1_out0), .OUT1(processor_enabler_1_out1),
    .OUT2(processor_enabler_1_out2), .OUT3(processor_enabler_1_out3), .OUT4(processor_enabler_1_out4),
    .OUT5(processor_enabler_1_out5), .OUT6(processor_enabler_1_out6), .OUT7(processor_enabler_1_out7));
  Intel_Adder_Inside intel_adder_inside_1 (
    .c(button_1_out), .a0(processor_enabler_1_out0), .a1(processor_enabler_1_out1),
    .a2(processor_enabler_1_out2), .a3(processor_enabler_1_out3), .a4(processor_enabler_1_out4),
    .a5(processor_enabler_1_out5), .b0(processor_enabler_aux_1_out0), .a6(processor_enabler_1_out6),
    .b1(processor_enabler_aux_1_out1), .a7(processor_enabler_1_out7), .b2(processor_enabler_aux_1_out2),
    .b4(processor_enabler_aux_1_out4), .b5(processor_enabler_aux_1_out5), .b3(processor_enabler_aux_1_out3),
    .b6(processor_enabler_aux_1_out6), .b7(processor_enabler_aux_1_out7), .Resto(intel_adder_inside_1_resto),
    .y0(intel_adder_inside_1_y0[0]), .y1(intel_adder_inside_1_y0[1]), .y2(intel_adder_inside_1_y0[2]),
    .y3(intel_adder_inside_1_y0[3]), .y4(intel_adder_inside_1_y0[4]), .y5(intel_adder_inside_1_y0[5]),
    .y6(intel_adder_inside_1_y0[6]), .y7(intel_adder_inside_1_y0[7]));
  Processor_Enabler_AUX processor_enabler_aux_1 (
    .Processor_Check(arith_unit_operation_select_1_somma), .IN0(b0), .IN1(b1), .IN2(b2), .IN3(b3), .IN4(b4),
    .IN5(b5), .IN6(b6), .IN7(b7), .OUT0(processor_enabler_aux_1_out0), .OUT1(processor_enabler_aux_1_out1),
    .OUT2(processor_enabler_aux_1_out2), .OUT3(processor_enabler_aux_1_out3),
    .OUT4(processor_enabler_aux_1_out4), .OUT5(processor_enabler_aux_1_out5),
    .OUT6(processor_enabler_aux_1_out6), .OUT7(processor_enabler_aux_1_out7));
  Processor_Enabler processor_enabler_2 (
    .Processor_Check(arith_unit_operation_select_1_sottrazione), .IN0(a0), .IN1(a1), .IN2(a2), .IN3(a3),
    .IN4(a4), .IN5(a5), .IN6(a6), .IN7(a7), .OUT0(processor_enabler_2_out0), .OUT1(processor_enabler_2_out1),
    .OUT2(processor_enabler_2_out2), .OUT3(processor_enabler_2_out3), .OUT4(processor_enabler_2_out4),
    .OUT5(processor_enabler_2_out5), .OUT6(processor_enabler_2_out6), .OUT7(processor_enabler_2_out7));
  Cpl2 cpl2_1 (
    .a0(processor_enabler_2_out0), .a1(processor_enabler_2_out1), .a2(processor_enabler_2_out2),
    .a3(processor_enabler_2_out3), .a4(processor_enabler_2_out4), .a5(processor_enabler_2_out5),
    .a6(processor_enabler_2_out6), .a7(processor_enabler_2_out7), .b0(processor_enabler_aux_2_out0),
    .b1(processor_enabler_aux_2_out1), .b2(processor_enabler_aux_2_out2), .b3(processor_enabler_aux_2_out3),
    .b4(processor_enabler_aux_2_out4), .b5(processor_enabler_aux_2_out5), .b6(processor_enabler_aux_2_out6),
    .b7(processor_enabler_aux_2_out7), .y0(cpl2_1_y0[0]), .y1(cpl2_1_y0[1]), .y2(cpl2_1_y0[2]),
    .y3(cpl2_1_y0[3]), .y4(cpl2_1_y0[4]), .y5(cpl2_1_y0[5]), .y6(cpl2_1_y0[6]), .y7(cpl2_1_y0[7]),
    .c(button_1_out));  // open: OVER
  Processor_Enabler_AUX processor_enabler_aux_2 (
    .Processor_Check(arith_unit_operation_select_1_sottrazione), .IN0(b0), .IN1(b1), .IN2(b2), .IN3(b3),
    .IN4(b4), .IN5(b5), .IN6(b6), .IN7(b7), .OUT0(processor_enabler_aux_2_out0),
    .OUT1(processor_enabler_aux_2_out1), .OUT2(processor_enabler_aux_2_out2),
    .OUT3(processor_enabler_aux_2_out3), .OUT4(processor_enabler_aux_2_out4),
    .OUT5(processor_enabler_aux_2_out5), .OUT6(processor_enabler_aux_2_out6),
    .OUT7(processor_enabler_aux_2_out7));
  Processor_Enabler processor_enabler_3 (
    .Processor_Check(arith_unit_operation_select_1_increm), .IN0(b0), .IN1(b1), .IN2(b2), .IN3(b3), .IN4(b4),
    .IN5(b5), .IN6(b6), .IN7(b7), .OUT0(processor_enabler_3_out0), .OUT1(processor_enabler_3_out1),
    .OUT2(processor_enabler_3_out2), .OUT3(processor_enabler_3_out3), .OUT4(processor_enabler_3_out4),
    .OUT5(processor_enabler_3_out5), .OUT6(processor_enabler_3_out6), .OUT7(processor_enabler_3_out7));
  B_increment b_increment_1 (
    .Carry(b_increment_1_carry), .B_1(b_increment_1_b_1), ._0(processor_enabler_3_out0),
    .in_2(processor_enabler_3_out1), .in_3(processor_enabler_3_out2), .in_4(processor_enabler_3_out3),
    .in_5(processor_enabler_3_out4), .in_6(processor_enabler_3_out5), .in_7(processor_enabler_3_out6),
    .in_8(processor_enabler_3_out7), .in_9(arith_unit_operation_select_1_increm));
  assign A = intel_adder_inside_1_y0 | cpl2_1_y0 | b_increment_1_b_1 | b_decrement_1_risultato | a_1_a;  // OR_Gate or_2, 8 bits wide
  or or_3 (or_3_out, intel_adder_inside_1_resto, b_increment_1_carry);
  Processor_Enabler processor_enabler_4 (
    .Processor_Check(arith_unit_operation_select_1_decrem), .IN0(b0), .IN1(b1), .IN2(b2), .IN3(b3), .IN4(b4),
    .IN5(b5), .IN6(b6), .IN7(b7), .OUT0(processor_enabler_4_out0), .OUT1(processor_enabler_4_out1),
    .OUT2(processor_enabler_4_out2), .OUT3(processor_enabler_4_out3), .OUT4(processor_enabler_4_out4),
    .OUT5(processor_enabler_4_out5), .OUT6(processor_enabler_4_out6), .OUT7(processor_enabler_4_out7));
  B_decrement b_decrement_1 (
    .Risultato(b_decrement_1_risultato), ._0(processor_enabler_4_out0), .in_2(processor_enabler_4_out1),
    .in_3(processor_enabler_4_out2), .in_4(processor_enabler_4_out3), .in_5(processor_enabler_4_out4),
    .in_6(processor_enabler_4_out5), .in_7(processor_enabler_4_out6), .in_8(processor_enabler_4_out7),
    .Abilit(arith_unit_operation_select_1_decrem));  // open: Carry
  Arith_Status_Check arith_status_check_1 (.C(or_3_out), .RE(A), .V(V), .C_2(C), .Z(arith_status_check_1_z), .N(N));
  and and_1 (Z, arith_status_check_1_z, or_1_out);
endmodule

module LogicUnit (
  input  _0,
  input  in_2,
  input  _3,
  input  [7:0] A,
  input  [7:0] B,
  output [7:0] Logic_Out,
  output Z,
  output C,
  output N
);

  wire arith_status_check_1_c_2, arith_status_check_1_n, arith_status_check_1_z,
       logic_unit_operation_select_1_and, logic_unit_operation_select_1_not,
       logic_unit_operation_select_1_or, logic_unit_operation_select_1_sd, logic_unit_operation_select_1_ss,
       or_1_out, or_2_out, schift_1_cdx;
  wire [7:0] and_8_bit_1_y_and, logic_output_authenticator_1_out, logic_output_authenticator_2_out,
       logic_output_authenticator_3_out, logicunit_abilitator_1_uscita, logicunit_abilitator_2_uscita,
       logicunit_abilitator_3_uscita, logicunit_abilitator_4_uscita, logicunit_abilitator_5_uscita,
       logicunit_abilitator_6_uscita, logicunit_abilitator_7_uscita, not_8_bit_1_b_negato, or_8_bit_1_y_or,
       schift_1_dx_2, schift_1_sx_2;

  or or_1 (or_1_out, logic_unit_operation_select_1_and, logic_unit_operation_select_1_or, logic_unit_operation_select_1_not, logic_unit_operation_select_1_ss);
  Logic_Unit_Operation_Select logic_unit_operation_select_1 (
    ._0(_0), .in_2(in_2), ._2(_3), .And(logic_unit_operation_select_1_and),
    .Or(logic_unit_operation_select_1_or), .Not(logic_unit_operation_select_1_not),
    .SS(logic_unit_operation_select_1_ss), .SD(logic_unit_operation_select_1_sd));
  LogicUnit_Abilitator logicunit_abilitator_1 (
    .Ingresso(A), .Abi(logic_unit_operation_select_1_and), .Uscita(logicunit_abilitator_1_uscita));
  LogicUnit_Abilitator logicunit_abilitator_2 (
    .Ingresso(B), .Abi(logic_unit_operation_select_1_and), .Uscita(logicunit_abilitator_2_uscita));
  LogicUnit_Abilitator logicunit_abilitator_3 (
    .Ingresso(A), .Abi(logic_unit_operation_select_1_or), .Uscita(logicunit_abilitator_3_uscita));
  LogicUnit_Abilitator logicunit_abilitator_4 (
    .Ingresso(B), .Abi(logic_unit_operation_select_1_or), .Uscita(logicunit_abilitator_4_uscita));
  LogicUnit_Abilitator logicunit_abilitator_5 (
    .Ingresso(B), .Abi(logic_unit_operation_select_1_not), .Uscita(logicunit_abilitator_5_uscita));
  LogicUnit_Abilitator logicunit_abilitator_6 (
    .Ingresso(B), .Abi(logic_unit_operation_select_1_sd), .Uscita(logicunit_abilitator_6_uscita));
  LogicUnit_Abilitator logicunit_abilitator_7 (
    .Ingresso(B), .Abi(logic_unit_operation_select_1_ss), .Uscita(logicunit_abilitator_7_uscita));
  Schift schift_1 (
    .DX(logicunit_abilitator_6_uscita), .SX(logicunit_abilitator_7_uscita), .CDX(schift_1_cdx),
    .DX_2(schift_1_dx_2), .SX_2(schift_1_sx_2), .CSX(schift_1_cdx));
  or or_2 (or_2_out, logic_unit_operation_select_1_sd, logic_unit_operation_select_1_ss);
  And_8_bit and_8_bit_1 (
    .A_and(logicunit_abilitator_1_uscita), .B_and(logicunit_abilitator_2_uscita), .Y_and(and_8_bit_1_y_and));
  Logic_Output_Authenticator logic_output_authenticator_1 (
    .in_1(or_8_bit_1_y_or), .in_2(logic_unit_operation_select_1_or), .Out(logic_output_authenticator_1_out));
  Or_8_bit or_8_bit_1 (
    .A_or(logicunit_abilitator_3_uscita), .B_or(logicunit_abilitator_4_uscita), .Y_or(or_8_bit_1_y_or));
  Not_8_bit not_8_bit_1 (.B(logicunit_abilitator_5_uscita), .B_negato(not_8_bit_1_b_negato));
  Logic_Output_Authenticator logic_output_authenticator_2 (
    .in_1(and_8_bit_1_y_and), .in_2(logic_unit_operation_select_1_and), .Out(logic_output_authenticator_2_out));
  Logic_Output_Authenticator logic_output_authenticator_3 (
    .in_1(not_8_bit_1_b_negato), .in_2(logic_unit_operation_select_1_not),
    .Out(logic_output_authenticator_3_out));
  assign Logic_Out = logic_output_authenticator_2_out | logic_output_authenticator_1_out | logic_output_authenticator_3_out | schift_1_dx_2 | schift_1_sx_2;  // OR_Gate or_3, 8 bits wide
  Arith_Status_Check arith_status_check_1 (
    .C(schift_1_cdx), .RE(Logic_Out), .C_2(arith_status_check_1_c_2), .Z(arith_status_check_1_z),
    .N(arith_status_check_1_n));  // open: V
  and and_1 (C, arith_status_check_1_c_2, or_2_out);
  and and_2 (N, arith_status_check_1_n, or_2_out);
  and and_3 (Z, arith_status_check_1_z, or_1_out);
endmodule

module Cpl2 (
  input  a0,
  input  a1,
  input  a2,
  input  a3,
  input  a4,
  input  a5,
  input  a6,
  input  a7,
  input  b0,
  input  c,
  input  b1,
  input  b2,
  input  b3,
  input  b4,
  input  b5,
  input  b6,
  input  b7,
  output OVER,
  output y0,
  output y1,
  output y2,
  output y3,
  output y4,
  output y5,
  output y6,
  output y7
);

  wire intel_adder_inside_1_y0, intel_adder_inside_1_y1, intel_adder_inside_1_y2, intel_adder_inside_1_y3,
       intel_adder_inside_1_y4, intel_adder_inside_1_y5, intel_adder_inside_1_y6, intel_adder_inside_1_y7,
       not_1_out, not_2_out, not_3_out, not_4_out, not_5_out, not_6_out, not_7_out, not_8_out;

  not not_1 (not_1_out, b0);
  not not_2 (not_2_out, b1);
  not not_3 (not_3_out, b2);
  not not_4 (not_4_out, b3);
  not not_5 (not_5_out, b4);
  not not_6 (not_6_out, b5);
  not not_7 (not_7_out, b6);
  not not_8 (not_8_out, b7);
  Intel_Adder_Inside intel_adder_inside_1 (
    .c(1'b0), .a0(1'b1), .a1(1'b0), .a2(1'b0), .a3(1'b0), .a4(1'b0), .a5(1'b0), .b0(not_1_out), .a6(1'b0),
    .b1(not_2_out), .a7(1'b0), .b2(not_3_out), .b4(not_5_out), .b5(not_6_out), .b3(not_4_out),
    .b6(not_7_out), .b7(not_8_out), .y0(intel_adder_inside_1_y0), .y1(intel_adder_inside_1_y1),
    .y2(intel_adder_inside_1_y2), .y3(intel_adder_inside_1_y3), .y4(intel_adder_inside_1_y4),
    .y5(intel_adder_inside_1_y5), .y6(intel_adder_inside_1_y6), .y7(intel_adder_inside_1_y7));  // open: Resto
  Intel_Adder_Inside intel_adder_inside_2 (
    .c(c), .a0(a0), .a1(a1), .a2(a2), .a3(a3), .a4(a4), .a5(a5), .b0(intel_adder_inside_1_y0), .a6(a6),
    .b1(intel_adder_inside_1_y1), .a7(a7), .b2(intel_adder_inside_1_y2), .b4(intel_adder_inside_1_y4),
    .b5(intel_adder_inside_1_y5), .b3(intel_adder_inside_1_y3), .b6(intel_adder_inside_1_y6),
    .b7(intel_adder_inside_1_y7), .Resto(OVER), .y0(y0), .y1(y1), .y2(y2), .y3(y3), .y4(y4), .y5(y5),
    .y6(y6), .y7(y7));
endmodule

// Integrated Processor Enabler
module Processor_Enabler (
  input  IN0,
  input  IN1,
  input  IN2,
  input  IN3,
  input  IN4,
  input  IN5,
  input  IN6,
  input  IN7,
  input  Processor_Check,
  output OUT0,
  output OUT1,
  output OUT2,
  output OUT3,
  output OUT4,
  output OUT5,
  output OUT6,
  output OUT7
);

  and and_1 (OUT1, Processor_Check, IN1);
  and and_2 (OUT0, Processor_Check, IN0);
  and and_3 (OUT2, Processor_Check, IN2);
  and and_4 (OUT4, Processor_Check, IN4);
  and and_5 (OUT3, Processor_Check, IN3);
  and and_6 (OUT5, Processor_Check, IN5);
  and and_7 (OUT7, Processor_Check, IN7);
  and and_8 (OUT6, Processor_Check, IN6);
endmodule

// Integrated Processor Enabler
module Processor_Enabler_AUX (
  input  IN0,
  input  IN1,
  input  IN2,
  input  IN3,
  input  IN4,
  input  IN5,
  input  IN6,
  input  IN7,
  input  Processor_Check,
  output OUT0,
  output OUT1,
  output OUT2,
  output OUT3,
  output OUT4,
  output OUT5,
  output OUT6,
  output OUT7
);

  and and_1 (OUT1, Processor_Check, IN1);
  and and_2 (OUT0, Processor_Check, IN0);
  and and_3 (OUT2, Processor_Check, IN2);
  and and_4 (OUT5, Processor_Check, IN5);
  and and_5 (OUT3, Processor_Check, IN3);
  and and_6 (OUT4, Processor_Check, IN4);
  and and_7 (OUT7, Processor_Check, IN7);
  and and_8 (OUT6, Processor_Check, IN6);
endmodule

// OPA
module Operation_Selector (
  input  I0,
  input  I1,
  output S0,
  output S1,
  output S2,
  output S3
);

  wire not_1_out, not_2_out;

  not not_1 (not_1_out, I0);
  not not_2 (not_2_out, I1);
  and and_1 (S0, not_1_out, not_2_out);
  and and_2 (S1, not_1_out, I1);
  and and_3 (S2, not_2_out, I0);
  and and_4 (S3, I1, I0);
endmodule

// Integrated Result Confirmer
module Result_Confirmer (
  input  a0,
  input  a1,
  input  a2,
  input  a3,
  input  a4,
  input  a5,
  input  a6,
  input  a7,
  input  b0,
  input  b1,
  input  b2,
  input  b3,
  input  b4,
  input  b5,
  input  b6,
  input  b7,
  output [7:0] out_17
);

  or or_1 (out_17[0], a0, b0);
  or or_2 (out_17[1], a1, b1);
  or or_3 (out_17[2], a2, b2);
  or or_4 (out_17[3], a3, b3);
  or or_5 (out_17[4], a4, b4);
  or or_6 (out_17[5], a5, b5);
  or or_7 (out_17[6], a6, b6);
  or or_8 (out_17[7], a7, b7);
endmodule

module Intel_Adder_Inside (
  input  c,
  input  a0,
  input  a1,
  input  a2,
  input  a3,
  input  a4,
  input  a5,
  input  b0,
  input  a6,
  input  b1,
  input  a7,
  input  b2,
  input  b4,
  input  b5,
  input  b3,
  input  b6,
  input  b7,
  output Resto,
  output y0,
  output y1,
  output y2,
  output y3,
  output y4,
  output y5,
  output y6,
  output y7
);

  wire n4_bit_adder_processor_1_c_2;

  _4_bit_adder_processor u_4_bit_adder_processor_1 (
    .c(c), .a0(a0), .a1(a1), .a2(a2), .a3(a3), .b0(b0), .b1(b1), .b2(b2), .b3(b3), .s0(y0), .s1(y1), .s2(y2),
    .s3(y3), .C_2(n4_bit_adder_processor_1_c_2));
  _4_bit_adder_processor u_4_bit_adder_processor_2 (
    .c(n4_bit_adder_processor_1_c_2), .a0(a4), .a1(a5), .a2(a6), .a3(a7), .b0(b4), .b1(b5), .b2(b6), .b3(b7),
    .s0(y4), .s1(y5), .s2(y6), .s3(y7), .C_2(Resto));
endmodule

module Full_Adder_Subsystem (
  input  c0,
  input  a,
  input  b,
  output S,
  output C
);

  wire and_1_out, and_2_out, and_3_out, xor_1_out;

  and and_1 (and_1_out, b, a);
  xor xor_1 (xor_1_out, a, b);
  xor xor_2 (S, xor_1_out, c0);
  and and_2 (and_2_out, c0, b);
  and and_3 (and_3_out, c0, a);
  or or_1 (C, and_1_out, and_3_out, and_2_out);
endmodule

module _4_bit_adder_processor (
  input  c,
  input  a0,
  input  a1,
  input  a2,
  input  a3,
  input  b0,
  input  b1,
  input  b2,
  input  b3,
  output s0,
  output s1,
  output s2,
  output s3,
  output C_2
);

  wire full_adder_subsystem_1_c, full_adder_subsystem_2_c, full_adder_subsystem_3_c;

  Full_Adder_Subsystem full_adder_subsystem_1 (.c0(c), .a(a0), .b(b0), .S(s0), .C(full_adder_subsystem_1_c));
  Full_Adder_Subsystem full_adder_subsystem_2 (
    .c0(full_adder_subsystem_1_c), .a(a1), .b(b1), .S(s1), .C(full_adder_subsystem_2_c));
  Full_Adder_Subsystem full_adder_subsystem_3 (
    .c0(full_adder_subsystem_2_c), .a(a2), .b(b2), .S(s2), .C(full_adder_subsystem_3_c));
  Full_Adder_Subsystem full_adder_subsystem_4 (.c0(full_adder_subsystem_3_c), .a(a3), .b(b3), .S(s3), .C(C_2));
endmodule

module Decoder (
  input  O0,
  input  O1,
  input  O2,
  output I7_2600K,
  output I6,
  output I5,
  output I4,
  output I3,
  output I2,
  output I1,
  output I0
);

  wire not_1_out, not_2_out, not_3_out;

  not not_1 (not_1_out, O0);
  not not_2 (not_2_out, O1);
  not not_3 (not_3_out, O2);
  and and_1 (I7_2600K, O0, O1, O2);
  and and_2 (I6, O0, O1, not_3_out);
  and and_3 (I5, O0, not_2_out, O2);
  and and_4 (I4, O0, not_2_out, not_3_out);
  and and_5 (I2, not_1_out, O1, not_3_out);
  and and_6 (I3, not_1_out, O1, O2);
  and and_7 (I1, not_1_out, not_2_out, O2);
  and and_8 (I0, not_1_out, not_2_out, not_3_out);
endmodule

// LUA
module LogicUnit_Abilitator (
  input  [7:0] Ingresso,
  input  Abi,
  output [7:0] Uscita
);

  and and_1 (Uscita[0], Abi, Ingresso[0]);
  and and_2 (Uscita[2], Abi, Ingresso[2]);
  and and_3 (Uscita[1], Abi, Ingresso[1]);
  and and_4 (Uscita[3], Abi, Ingresso[3]);
  and and_5 (Uscita[5], Abi, Ingresso[5]);
  and and_6 (Uscita[4], Abi, Ingresso[4]);
  and and_7 (Uscita[7], Abi, Ingresso[7]);
  and and_8 (Uscita[6], Abi, Ingresso[6]);
endmodule

// AOS
module Arith_Unit_Operation_Select (
  input  _0,
  input  _1,
  input  _2,
  input  _3,
  output Somma,
  output Sottrazione,
  output Increm,
  output Decrem,
  output aBlank
);

  wire not_1_out, not_2_out, not_3_out, not_4_out, not_5_out, not_6_out, not_7_out, not_8_out;

  not not_1 (not_1_out, _1);
  not not_2 (not_2_out, _3);
  not not_3 (not_3_out, _0);
  not not_4 (not_4_out, _1);
  not not_5 (not_5_out, _2);
  not not_6 (not_6_out, not_1_out);
  not not_7 (not_7_out, _0);
  not not_8 (not_8_out, _3);
  and and_1 (Sottrazione, not_6_out, not_7_out, _2, _1);
  and and_2 (Increm, _0, _2, _1, not_8_out);
  and and_3 (Decrem, not_3_out, not_4_out, not_5_out, _3);
  and and_4 (aBlank, _0, not_5_out, not_4_out, _3);
  and and_5 (Somma, _0, not_1_out, _2, not_2_out);
endmodule

module B_increment (
  input  _0,
  input  in_2,
  input  in_3,
  input  in_4,
  input  in_5,
  input  in_6,
  input  in_7,
  input  in_8,
  input  in_9,
  output Carry,
  output [7:0] B_1
);

  Intel_Adder_Inside intel_adder_inside_1 (
    .c(in_9), .a0(_0), .a1(in_2), .a2(in_3), .a3(in_4), .a4(in_5), .a5(in_6), .b0(1'b0), .a6(in_7),
    .b1(1'b0), .a7(in_8), .b2(1'b0), .b4(1'b0), .b5(1'b0), .b3(1'b0), .b6(1'b0), .b7(1'b0), .Resto(Carry),
    .y0(B_1[0]), .y1(B_1[1]), .y2(B_1[2]), .y3(B_1[3]), .y4(B_1[4]), .y5(B_1[5]), .y6(B_1[6]), .y7(B_1[7]));
endmodule

module B_decrement (
  input  _0,
  input  in_2,
  input  in_3,
  input  in_4,
  input  in_5,
  input  in_6,
  input  in_7,
  input  in_8,
  input  Abilit,
  output [7:0] Risultato,
  output Carry
);

  Cpl2 cpl2_1 (
    .a0(_0), .a1(in_2), .a2(in_3), .a3(in_4), .a4(in_5), .a5(in_6), .a6(in_7), .a7(in_8), .b0(Abilit),
    .b1(1'b0), .b2(1'b0), .b3(1'b0), .b4(1'b0), .b5(1'b0), .b6(1'b0), .b7(1'b0), .y0(Risultato[0]),
    .y1(Risultato[1]), .y2(Risultato[2]), .y3(Risultato[3]), .y4(Risultato[4]), .y5(Risultato[5]),
    .y6(Risultato[6]), .y7(Risultato[7]), .c(1'b0), .OVER(Carry));
endmodule

module A (
  input  [7:0] in_1,
  input  in_2,
  output [7:0] A
);

  assign A = in_1 & {8{in_2}};  // AND_Gate and_1, 8 bits wide
endmodule

module Arith_Status_Check (
  input  C,
  input  [7:0] RE,
  output V,
  output C_2,
  output Z,
  output N
);

  wire or_1_out;

  xor xor_1 (V, C, RE[7]);
  or or_1 (or_1_out, RE[0], RE[1], RE[2], RE[3], RE[4], RE[5], RE[6], RE[7]);
  not not_1 (Z, or_1_out);

  assign C_2 = C;
  assign N = RE[7];
endmodule

module And_8_bit (
  input  [7:0] A_and,
  input  [7:0] B_and,
  output [7:0] Y_and
);

  assign Y_and = A_and & B_and;  // AND_Gate and_1, 8 bits wide
endmodule

module Or_8_bit (
  input  [7:0] A_or,
  input  [7:0] B_or,
  output [7:0] Y_or
);

  assign Y_or = A_or | B_or;  // OR_Gate or_1, 8 bits wide
endmodule

module Not_8_bit (
  input  [7:0] B,
  output [7:0] B_negato
);

  assign B_negato = ~B;  // NOT_Gate not_1, 8 bits wide
endmodule

module Schift (
  input  [7:0] DX,
  input  [7:0] SX,
  output CDX,
  output [7:0] DX_2,
  output [7:0] SX_2,
  output CSX
);


  assign CDX = DX[0];
  assign CSX = SX[7];
  assign DX_2 = {1'b0, DX[7:1]};
  assign SX_2 = {SX[6:0], 1'b0};
endmodule

// LOS
module Logic_Unit_Operation_Select (
  input  _0,
  input  in_2,
  input  _2,
  output And,
  output Or,
  output Not,
  output SS,
  output SD
);

  wire not_1_out, not_2_out, not_3_out, not_4_out, not_5_out, not_6_out, not_7_out;

  not not_1 (not_1_out, _0);
  not not_2 (not_2_out, in_2);
  not not_3 (not_3_out, _2);
  and and_1 (And, not_1_out, not_2_out, not_3_out);
  and and_2 (Or, _0, not_3_out, not_2_out);
  not not_4 (not_4_out, not_2_out);
  and and_3 (Not, not_4_out, not_3_out, not_1_out);
  and and_4 (SS, _0, in_2, not_3_out);
  not not_5 (not_5_out, not_3_out);
  not not_6 (not_6_out, _0);
  and and_5 (SD, not_5_out, not_6_out, not_7_out);
  not not_7 (not_7_out, in_2);
endmodule

// LOA
module Logic_Output_Authenticator (
  input  [7:0] in_1,
  input  in_2,
  output [7:0] Out
);

  assign Out = in_1 & {8{in_2}};  // AND_Gate and_1, 8 bits wide
endmodule

module Instant_Calc_Memory (
  input  [7:0] From_Calc_Unit,
  input  Save,
  input  Clear,
  output [7:0] From_Volatile_Memory
);

  wire mux_1_to_memory, mux_2_to_memory, mux_3_to_memory, mux_4_to_memory, mux_5_to_memory, mux_6_to_memory,
       mux_7_to_memory;

  D_Flip_Flop d_ff_1 (
    .clk(Save), .D(From_Calc_Unit[7]), .Q(From_Volatile_Memory[7]), .reset(Clear));  // open: Qn, preset, en
  Mux mux_1 (
    .From_Parallel(From_Calc_Unit[6]), .From_Serial(From_Volatile_Memory[7]), .To_memory(mux_1_to_memory),
    .Control(1'b0));
  D_Flip_Flop d_ff_2 (
    .clk(Save), .D(mux_1_to_memory), .Q(From_Volatile_Memory[6]), .reset(Clear));  // open: Qn, preset, en
  Mux mux_2 (
    .From_Parallel(From_Calc_Unit[5]), .From_Serial(From_Volatile_Memory[6]), .To_memory(mux_2_to_memory),
    .Control(1'b0));
  D_Flip_Flop d_ff_3 (
    .clk(Save), .D(mux_2_to_memory), .Q(From_Volatile_Memory[5]), .reset(Clear));  // open: Qn, preset, en
  Mux mux_3 (
    .From_Parallel(From_Calc_Unit[4]), .From_Serial(From_Volatile_Memory[5]), .To_memory(mux_3_to_memory),
    .Control(1'b0));
  D_Flip_Flop d_ff_4 (
    .clk(Save), .D(mux_3_to_memory), .Q(From_Volatile_Memory[4]), .reset(Clear));  // open: Qn, preset, en
  Mux mux_4 (
    .From_Parallel(From_Calc_Unit[3]), .From_Serial(From_Volatile_Memory[4]), .To_memory(mux_4_to_memory),
    .Control(1'b0));
  D_Flip_Flop d_ff_5 (
    .clk(Save), .D(mux_4_to_memory), .Q(From_Volatile_Memory[3]), .reset(Clear));  // open: Qn, preset, en
  Mux mux_5 (
    .From_Parallel(From_Calc_Unit[2]), .From_Serial(From_Volatile_Memory[3]), .To_memory(mux_5_to_memory),
    .Control(1'b0));
  Mux mux_6 (
    .From_Parallel(From_Calc_Unit[1]), .From_Serial(From_Volatile_Memory[2]), .To_memory(mux_6_to_memory),
    .Control(1'b0));
  D_Flip_Flop d_ff_6 (
    .clk(Save), .D(mux_5_to_memory), .Q(From_Volatile_Memory[2]), .reset(Clear));  // open: Qn, preset, en
  D_Flip_Flop d_ff_7 (
    .clk(Save), .D(mux_6_to_memory), .Q(From_Volatile_Memory[1]), .reset(Clear));  // open: Qn, preset, en
  Mux mux_7 (
    .From_Parallel(From_Calc_Unit[0]), .From_Serial(From_Volatile_Memory[1]), .To_memory(mux_7_to_memory),
    .Control(1'b0));
  D_Flip_Flop d_ff_8 (
    .clk(Save), .D(mux_7_to_memory), .Q(From_Volatile_Memory[0]), .reset(Clear));  // open: Qn, preset, en
endmodule

module Mux (
  input  From_Parallel,
  input  From_Serial,
  input  Control,
  output To_memory
);

  wire and_1_out, and_2_out, not_1_out;

  not not_1 (not_1_out, Control);
  and and_1 (and_1_out, From_Parallel, not_1_out);
  or or_1 (To_memory, and_1_out, and_2_out);
  and and_2 (and_2_out, From_Serial, Control);
endmodule
